# Fritzing sketch anpan_melody2_circuit_diagram (saved by Fritzing 0.9.3b)
breadboards: 1

parts:
  R1 = Resistor [tolerance=±5% resistance=150 package=THT]
  R2 = Resistor [tolerance=±5% resistance=150 package=THT]
  R3 = Resistor [tolerance=±5% resistance=150 package=THT]
  Speaker = Piezo Speaker
  LED1 = RGB LED (com. cathode, rgb) [package="5 mm [THT]"]
  S1 = Square Pushbutton
  waves_Arduino_Pro_Mini_互換ボード_328_5V_16MHz = Arduino Pro Mini v13
  V1 = DC Power [voltage=5]
  Switch1 = SWITCH-SPST-2 [package=switch-spst-vertical]
  Switch2 = SWITCH-SPST-2 [package=switch-spst-vertical]
  Switch3 = SWITCH-SPST-2 [package=switch-spst-vertical]

nets:
  N1: R1.Pin_0, waves_Arduino_Pro_Mini_互換ボード_328_5V_16MHz.D3_PWM
  N2: R1.Pin_1, LED1.red_anode
  N3: R2.Pin_0, waves_Arduino_Pro_Mini_互換ボード_328_5V_16MHz.D4
  N4: R2.Pin_1, LED1.green_anode
  N5: R3.Pin_0, waves_Arduino_Pro_Mini_互換ボード_328_5V_16MHz.D5_PWM
  N6: R3.Pin_1, LED1.blue_anode
  N7: Speaker.pin1, waves_Arduino_Pro_Mini_互換ボード_328_5V_16MHz.D2
  N8: Speaker.pin2, waves_Arduino_Pro_Mini_互換ボード_328_5V_16MHz.GND, V1.V-, Switch1.O, Switch2.O, Switch3.O
  N9: LED1.common_cathode, waves_Arduino_Pro_Mini_互換ボード_328_5V_16MHz.VCC
  N10: S1.leg0, V1.V+
  N11: S1.leg1, waves_Arduino_Pro_Mini_互換ボード_328_5V_16MHz.RAW
  N12: waves_Arduino_Pro_Mini_互換ボード_328_5V_16MHz.D8, Switch3.P
  N13: waves_Arduino_Pro_Mini_互換ボード_328_5V_16MHz.D7, Switch2.P
  N14: waves_Arduino_Pro_Mini_互換ボード_328_5V_16MHz.D6_PWM, Switch1.P
