# Fritzing sketch autosanitizer2 (saved by Fritzing 0.9.3b)
breadboards: 1

parts:
  J1 = Basic Servo
  VCC1 = 4 x AAA Battery Mount
  LCD1 = LCD screen
  R3 = Rotary Potentiometer (Small) [maximum_resistance=10kΩ package=THT]
  Arduino_pro_mini = Arduino Pro Mini v13
  R4 = Resistor [tolerance=±5% resistance=4.7k package=THT]
  R5 = Resistor [tolerance=±5% resistance=150 package=THT]
  HC-SR04_Sensor_1 = HC-SR04 Ultrasonic Distance Sensor

nets:
  GND: J1.gnd, VCC1.-, LCD1.VSS, LCD1.R/W, LCD1.LED-, R3.leg1, Arduino_pro_mini.GND, R4.Pin_1, HC-SR04_Sensor_1.ECHO
  N1: J1.vcc, VCC1.+, Arduino_pro_mini.RAW
  N2: J1.pulse, Arduino_pro_mini.D9_PWM
  VCC: LCD1.VDD, R3.leg2, Arduino_pro_mini.VCC, R5.Pin_1, HC-SR04_Sensor_1.VCC
  N3: LCD1.V0, R4.Pin_0
  N4: LCD1.RS, Arduino_pro_mini.D4
  N5: LCD1.E, Arduino_pro_mini.D6_PWM
  N6: LCD1.DB4, Arduino_pro_mini.D10_PWM/SS
  N7: LCD1.DB5, Arduino_pro_mini.D11_PWM/MOSI
  N8: LCD1.DB6, Arduino_pro_mini.D12/MISO
  N9: LCD1.DB7, Arduino_pro_mini.D13/SCK
  N10: LCD1.LED+, R5.Pin_0
  N11: R3.wiper, Arduino_pro_mini.A1
  N12: Arduino_pro_mini.D3_PWM, HC-SR04_Sensor_1.GND
  N13: Arduino_pro_mini.D2, HC-SR04_Sensor_1.TRIG
